// Logisim project fa1smschoolversion.circ as structural Verilog: 45 circuits, main circuit main
module main (
  input  input1,
  input  input2,
  input  a,
  input  b,
  output sum,
  output carry,
  output s,
  output cout
);

  wire nand_1_out, nor_1_out;

  nor nor_1 (nor_1_out, input1, input2);
  and and_1 (carry, input1, input2);
  nor nor_2 (sum, nor_1_out, carry);
  or or_1 (cout, a, b);
  nand nand_1 (nand_1_out, a, b);
  nand nand_2 (s, nand_1_out, cout);

  // Notes on the sheet:
  //   FA0 Ahantya Sharma
  //   2.75
  //   1.75
  //   14 transistors
  //   FA1 Ahantya Sharma
  //   1.75
  //   2.75
  //   14 transistors
endmodule

module fa0 (
  input  input1,
  input  input2,
  output sum,
  output carry
);

  wire nor_1_out;

  nor nor_1 (nor_1_out, input1, input2);
  and and_1 (carry, input1, input2);
  nor nor_2 (sum, nor_1_out, carry);

  // Notes on the sheet:
  //   FA0 Ahantya Sharma
  //   2.75
  //   1.75
  //   14 transistors
endmodule

module fa1 (
  input  a,
  input  b,
  output s,
  output cout
);

  wire nand_1_out;

  or or_1 (cout, a, b);
  nand nand_1 (nand_1_out, a, b);
  nand nand_2 (s, nand_1_out, cout);

  // Notes on the sheet:
  //   FA1 Ahantya Sharma
  //   1.75
  //   2.75
  //   14 transistors
endmodule

module FAopt1 (
  input  A,
  input  B,
  input  Cin,
  output S,
  output Cout
);

  wire nand_1_out, nand_2_out, nor_1_out, nor_2_out, nor_3_out, not_1_out, not_2_out;

  nor nor_1 (nor_1_out, A, B);
  not not_1 (not_1_out, nand_2_out);
  nor nor_2 (nor_2_out, nor_1_out, not_1_out);
  nand nand_1 (nand_1_out, nor_2_out, Cin);
  nand nand_2 (nand_2_out, A, B);
  nand nand_3 (Cout, nand_1_out, nand_2_out);
  nor nor_3 (nor_3_out, nor_2_out, Cin);
  not not_2 (not_2_out, nand_1_out);
  nor nor_4 (S, nor_3_out, not_2_out);

  // Notes on the sheet:
  //   32 transistors
  //   DELAY TO COUT: if Cin < 2.75 then 4.75, else Cin + 2  
  //   DELAY TO S: if Cin < 2.75 then 5.5, else Cin + 2.75 
endmodule

module FAOpt2 (
  input  A,
  input  B,
  input  Cin,
  output S,
  output Cout
);

  wire and_1_out, nand_1_out, nand_2_out, nand_3_out, nor_1_out, nor_2_out, nor_3_out, not_1_out;

  nand nand_1 (nand_1_out, A, Cin);
  nor nor_1 (nor_1_out, A, B);
  not not_1 (not_1_out, nand_3_out);
  nor nor_2 (nor_2_out, nor_1_out, not_1_out);
  nand nand_2 (nand_2_out, B, Cin);
  nand nand_3 (nand_3_out, A, B);
  nand nand_4 (Cout, nand_2_out, nand_1_out, nand_3_out);
  nor nor_3 (nor_3_out, nor_2_out, Cin);
  and and_1 (and_1_out, nor_2_out, Cin);
  nor nor_4 (S, nor_3_out, and_1_out);

  // Notes on the sheet:
  //   DELAY TO COUT: if Cin < 2.5 then < 4.75, else Cin + 2.25  
  //   DELAY TO S: if CIN < 2.75, then it is 5.5, then it is Cin + 2.75 
endmodule

module FourBitRippleCarryAdder0 (
  input  [3:0] a,
  input  [3:0] b,
  output [3:0] _8_75,
  output _8
);

  wire fa0_1_carry, faopt1_2_cout, faopt2_1_cout;

  FAopt1 faopt1_1 (.A(a[3]), .B(b[3]), .Cin(faopt1_2_cout), .Cout(_8), .S(_8_75[3]));
  FAopt1 faopt1_2 (.A(a[2]), .B(b[2]), .Cin(faopt2_1_cout), .Cout(faopt1_2_cout), .S(_8_75[2]));
  FAOpt2 faopt2_1 (.A(a[1]), .B(b[1]), .Cin(fa0_1_carry), .Cout(faopt2_1_cout), .S(_8_75[1]));
  fa0 fa0_1 (.input2(b[0]), .input1(a[0]), .carry(fa0_1_carry), .sum(_8_75[0]));

  // Notes on the sheet:
  //   0
  //   0
  //   8
  //   8.75
  //   120 transistors
  //   6
  //   6.75
  //   4
  //   5.5
  //   cout
  //   1.75
  //   2.75
endmodule

module FourBitRippleCarry1 (
  input  [3:0] a,
  input  [3:0] b,
  output [3:0] _8_75,
  output _8
);

  wire fa1_1_cout, faopt1_2_cout, faopt2_1_cout;

  FAopt1 faopt1_1 (.A(a[3]), .B(b[3]), .Cin(faopt1_2_cout), .Cout(_8), .S(_8_75[3]));
  FAopt1 faopt1_2 (.A(a[2]), .B(b[2]), .Cin(faopt2_1_cout), .Cout(faopt1_2_cout), .S(_8_75[2]));
  fa1 fa1_1 (.a(a[0]), .b(b[0]), .cout(fa1_1_cout), .s(_8_75[0]));
  FAOpt2 faopt2_1 (.A(a[1]), .B(b[1]), .Cin(fa1_1_cout), .Cout(faopt2_1_cout), .S(_8_75[1]));

  // Notes on the sheet:
  //   0
  //   0
  //   8
  //   8.75
  //   6
  //   6.75
  //   4
  //   5.5
  //   cout
  //   1.75
  //   2.75
endmodule

module EightBitRippleCarryAdder (
  input  [7:0] a_7_0_f0832ffb,
  input  [7:0] b_7_0_3e223e90,
  output [7:0] _16_75,
  output cout
);

  wire fa0_1_carry, faopt1_2_cout, faopt1_3_cout, faopt1_4_cout, faopt1_5_cout, faopt1_6_cout, faopt2_1_cout;

  FAopt1 faopt1_1 (.A(a_7_0_f0832ffb[7]), .B(b_7_0_3e223e90[7]), .Cin(faopt1_2_cout), .Cout(cout), .S(_16_75[7]));
  FAopt1 faopt1_2 (
    .A(a_7_0_f0832ffb[6]), .B(b_7_0_3e223e90[6]), .Cin(faopt1_3_cout), .Cout(faopt1_2_cout), .S(_16_75[6]));
  FAopt1 faopt1_3 (
    .A(a_7_0_f0832ffb[5]), .B(b_7_0_3e223e90[5]), .Cin(faopt1_4_cout), .Cout(faopt1_3_cout), .S(_16_75[5]));
  FAopt1 faopt1_4 (
    .A(a_7_0_f0832ffb[4]), .B(b_7_0_3e223e90[4]), .Cin(faopt1_5_cout), .Cout(faopt1_4_cout), .S(_16_75[4]));
  FAopt1 faopt1_5 (
    .A(a_7_0_f0832ffb[3]), .B(b_7_0_3e223e90[3]), .Cin(faopt1_6_cout), .Cout(faopt1_5_cout), .S(_16_75[3]));
  FAopt1 faopt1_6 (
    .A(a_7_0_f0832ffb[2]), .B(b_7_0_3e223e90[2]), .Cin(faopt2_1_cout), .Cout(faopt1_6_cout), .S(_16_75[2]));
  FAOpt2 faopt2_1 (
    .A(a_7_0_f0832ffb[1]), .B(b_7_0_3e223e90[1]), .Cin(fa0_1_carry), .Cout(faopt2_1_cout), .S(_16_75[1]));
  fa0 fa0_1 (.input2(b_7_0_3e223e90[0]), .input1(a_7_0_f0832ffb[0]), .carry(fa0_1_carry), .sum(_16_75[0]));

  // Notes on the sheet:
  //   0
  //   0
  //   16
  //   16.75
  //   248 transistors
  //   14
  //   14.75
  //   12
  //   12.75
  //   10
  //   8
  //   10.75
  //   8.75
  //   16
  //   6
  //   6.75
  //   4
  //   5.5
  //   1.75
  //   2.75
  //   8.75
endmodule

module L_2_to_1_Mux_90b0313b (
  input  in0,
  input  s,
  input  in1,
  output z
);

  wire nand_1_out, nand_2_out, not_1_out;

  not not_1 (not_1_out, s);
  nand nand_1 (nand_1_out, in0, not_1_out);
  nand nand_2 (nand_2_out, in1, s);
  nand nand_3 (z, nand_1_out, nand_2_out);

  // Notes on the sheet:
  //   z = max(s + 2.75, in0 + 2, + in1 + 2
endmodule

module L_4_to_1_mux_4fc587a3 (
  input  in_1,
  input  in_2,
  input  in_3,
  input  in_4,
  input  s1,
  input  s0,
  output out_7
);

  wire l_2_to_1_mux_90b0313b_1_z, l_2_to_1_mux_90b0313b_2_z;

  L_2_to_1_Mux_90b0313b l_2_to_1_mux_90b0313b_1 (.in0(in_1), .s(s0), .in1(in_2), .z(l_2_to_1_mux_90b0313b_1_z));
  L_2_to_1_Mux_90b0313b l_2_to_1_mux_90b0313b_2 (.in0(in_3), .s(s0), .in1(in_4), .z(l_2_to_1_mux_90b0313b_2_z));
  L_2_to_1_Mux_90b0313b l_2_to_1_mux_90b0313b_3 (
    .in0(l_2_to_1_mux_90b0313b_1_z), .s(s1), .in1(l_2_to_1_mux_90b0313b_2_z), .z(out_7));

  // Notes on the sheet:
  //   z = max(s0 + 4.75, s1 + 2.75, in0 + 4, in1 + 4, in2 + 4, in3 + 4)
endmodule

module mx2i (
  input  in0,
  input  in1,
  input  sel,
  output x1
);

  wire transmission_1_p3, transmission_1_p4;

  // Transmission_Gate transmission_1: pin names not known; wires that end beside it: in0, sel, transmission_1_p3, transmission_1_p4
  not not_1 (transmission_1_p3, sel);
  // Transmission_Gate transmission_2: pin names not known; wires that end beside it: in1, transmission_1_p3, sel, transmission_1_p4
  not not_2 (x1, transmission_1_p4);

  // Notes on the sheet:
  //   8 transistors
  //   z = max(s + 1.75, in0 + 1, in1 + 1)
endmodule

module mx4i (
  input  in0,
  input  in1,
  input  in2,
  input  in3,
  input  s0,
  input  s1,
  output z
);

  wire mx2i_1_x1, mx2i_2_x1;

  mx2i mx2i_1 (.sel(s0), .in0(in0), .in1(in1), .x1(mx2i_1_x1));
  mx2i mx2i_2 (.sel(s0), .in0(in2), .in1(in3), .x1(mx2i_2_x1));
  mx2i mx2i_3 (.sel(s1), .in0(mx2i_1_x1), .in1(mx2i_2_x1), .x1(z));

  // Notes on the sheet:
  //   z = max(s0 + 2.75, s1 + 1.75, in0 + 2, in1 + 2, in2 + 2, in3 + 2)
endmodule

module EightBitCarrySelectAdder0 (
  input  [7:0] a,
  input  [7:0] b,
  output [7:0] _10_5,
  output cout
);

  wire fourbitripplecarry1_1__8, fourbitripplecarryadder0_1__8, fourbitripplecarryadder0_2__8, mx2i_1_x1;
  wire [3:0] fourbitripplecarry1_1__8_75, fourbitripplecarryadder0_1__8_75, mx2i_4_1_zb_3_0;

  mx2i mx2i_1 (
    .sel(fourbitripplecarryadder0_2__8), .in0(fourbitripplecarryadder0_1__8), .in1(fourbitripplecarry1_1__8),
    .x1(mx2i_1_x1));
  not not_1 (cout, mx2i_1_x1);
  mx2i_4 mx2i_4_1 (
    .s(fourbitripplecarryadder0_2__8), .in_2(fourbitripplecarry1_1__8_75),
    .in_1(fourbitripplecarryadder0_1__8_75), .zb_3_0(mx2i_4_1_zb_3_0));
  assign _10_5[7:4] = ~mx2i_4_1_zb_3_0;  // NOT_Gate not_2, 4 bits wide
  FourBitRippleCarryAdder0 fourbitripplecarryadder0_1 (
    .a(a[7:4]), .b(b[7:4]), ._8(fourbitripplecarryadder0_1__8), ._8_75(fourbitripplecarryadder0_1__8_75));
  FourBitRippleCarry1 fourbitripplecarry1_1 (
    .a(a[7:4]), .b(b[7:4]), ._8(fourbitripplecarry1_1__8), ._8_75(fourbitripplecarry1_1__8_75));
  FourBitRippleCarryAdder0 fourbitripplecarryadder0_2 (
    .a(a[3:0]), .b(b[3:0]), ._8(fourbitripplecarryadder0_2__8), ._8_75(_10_5[3:0]));

  // Notes on the sheet:
  //   8
  //   8.75
  //   9.75
  //   8
  //   10.5
  //   8.75
  //   9.75
  //   8
  //   8.75
  //   sum
endmodule

module SixteenCarrySelectAdder (
  input  [15:0] a,
  input  [15:0] b,
  output [15:0] out_3,
  output _13
);

  wire eightbitcarryselectadder0_1_cout, eightbitcarryselectadder0_2_cout, eightbitcarryselectadder1_1_cout,
       mx2i_1_x1;
  wire [7:0] eightbitcarryselectadder0_1__10_5, eightbitcarryselectadder1_1__10_5, mx2i_8_1_out_4;

  mx2i mx2i_1 (
    .sel(eightbitcarryselectadder0_2_cout), .in0(eightbitcarryselectadder0_1_cout),
    .in1(eightbitcarryselectadder1_1_cout), .x1(mx2i_1_x1));
  not not_1 (_13, mx2i_1_x1);
  EightBitCarrySelectAdder1 eightbitcarryselectadder1_1 (
    .b(b[15:8]), .a(a[15:8]), .cout(eightbitcarryselectadder1_1_cout),
    ._10_5(eightbitcarryselectadder1_1__10_5));
  mx2i_8 mx2i_8_1 (
    .in_2(eightbitcarryselectadder1_1__10_5), .s(eightbitcarryselectadder0_2_cout),
    .in_1(eightbitcarryselectadder0_1__10_5), .out_4(mx2i_8_1_out_4));
  EightBitCarrySelectAdder0 eightbitcarryselectadder0_1 (
    .b(b[15:8]), .a(a[15:8]), .cout(eightbitcarryselectadder0_1_cout),
    ._10_5(eightbitcarryselectadder0_1__10_5));
  assign out_3[15:8] = ~mx2i_8_1_out_4;  // NOT_Gate not_2, 8 bits wide
  EightBitCarrySelectAdder0 eightbitcarryselectadder0_2 (
    .b(b[7:0]), .a(a[7:0]), .cout(eightbitcarryselectadder0_2_cout), ._10_5(out_3[7:0]));

  // Notes on the sheet:
  //   10.5
  //   12.25
  //   10.5
  //   10.5
  //   10.5
  //   10.5
  //   12.25
  //   10.5
  //   13
endmodule

module EightBitCarrySelectAdder1 (
  input  [7:0] a,
  input  [7:0] b,
  output [7:0] _10_5,
  output cout
);

  wire fourbitripplecarry1_1__8, fourbitripplecarry1_2__8, fourbitripplecarryadder0_1__8, mx2i_1_x1;
  wire [3:0] fourbitripplecarry1_1__8_75, fourbitripplecarryadder0_1__8_75, mx2i_4_1_zb_3_0;

  mx2i mx2i_1 (
    .sel(fourbitripplecarry1_2__8), .in0(fourbitripplecarryadder0_1__8), .in1(fourbitripplecarry1_1__8),
    .x1(mx2i_1_x1));
  not not_1 (cout, mx2i_1_x1);
  mx2i_4 mx2i_4_1 (
    .s(fourbitripplecarry1_2__8), .in_2(fourbitripplecarry1_1__8_75),
    .in_1(fourbitripplecarryadder0_1__8_75), .zb_3_0(mx2i_4_1_zb_3_0));
  assign _10_5[7:4] = ~mx2i_4_1_zb_3_0;  // NOT_Gate not_2, 4 bits wide
  FourBitRippleCarryAdder0 fourbitripplecarryadder0_1 (
    .a(a[7:4]), .b(b[7:4]), ._8(fourbitripplecarryadder0_1__8), ._8_75(fourbitripplecarryadder0_1__8_75));
  FourBitRippleCarry1 fourbitripplecarry1_1 (
    .a(a[7:4]), .b(b[7:4]), ._8(fourbitripplecarry1_1__8), ._8_75(fourbitripplecarry1_1__8_75));
  FourBitRippleCarry1 fourbitripplecarry1_2 (.a(a[3:0]), .b(b[3:0]), ._8(fourbitripplecarry1_2__8), ._8_75(_10_5[3:0]));

  // Notes on the sheet:
  //   8
  //   8.75
  //   9.75
  //   8
  //   10.5
  //   8.75
  //   9.75
  //   8
  //   8.75
  //   sum
endmodule

module mx2i_4 (
  input  [3:0] in_1,
  input  [3:0] in_2,
  input  s,
  output [3:0] zb_3_0
);

  mx2i mx2i_1 (.sel(s), .in0(in_1[0]), .in1(in_2[0]), .x1(zb_3_0[0]));
  mx2i mx2i_2 (.sel(s), .in0(in_1[1]), .in1(in_2[1]), .x1(zb_3_0[1]));
  mx2i mx2i_3 (.sel(s), .in0(in_1[2]), .in1(in_2[2]), .x1(zb_3_0[2]));
  mx2i mx2i_4 (.sel(s), .in0(in_1[3]), .in1(in_2[3]), .x1(zb_3_0[3]));
endmodule

module mx2i_8 (
  input  [7:0] in_1,
  input  [7:0] in_2,
  input  s,
  output [7:0] out_4
);

  mx2i mx2i_1 (.sel(s), .in0(in_1[0]), .in1(in_2[0]), .x1(out_4[0]));
  mx2i mx2i_2 (.sel(s), .in0(in_1[1]), .in1(in_2[1]), .x1(out_4[1]));
  mx2i mx2i_3 (.sel(s), .in0(in_1[2]), .in1(in_2[2]), .x1(out_4[2]));
  mx2i mx2i_4 (.sel(s), .in0(in_1[3]), .in1(in_2[3]), .x1(out_4[3]));
  mx2i mx2i_5 (.sel(s), .in0(in_1[4]), .in1(in_2[4]), .x1(out_4[4]));
  mx2i mx2i_6 (.sel(s), .in0(in_1[5]), .in1(in_2[5]), .x1(out_4[5]));
  mx2i mx2i_7 (.sel(s), .in0(in_1[6]), .in1(in_2[6]), .x1(out_4[6]));
  mx2i mx2i_8 (.sel(s), .in0(in_1[7]), .in1(in_2[7]), .x1(out_4[7]));
endmodule

module CLAC41 (
  input  G0,
  input  G1,
  input  G2,
  input  G3,
  input  P0,
  input  P1,
  input  P2,
  input  P3,
  input  C0,
  output out_10
);

  wire P3G2_out, P3P2G1_out, P3P2P1G0_out, P3P2P1P0C0_out;

  and P3G2 (P3G2_out, G2, P3);
  and P3P2G1 (P3P2G1_out, G1, P2, P3);
  and P3P2P1G0 (P3P2P1G0_out, G0, P1, P2, P3);
  and P3P2P1P0C0 (P3P2P1P0C0_out, P3, P2, P1, P0, C0);
  or or_1 (out_10, P3P2P1P0C0_out, P3P2P1G0_out, P3P2G1_out, P3G2_out, G3);
endmodule

module CLAC42 (
  input  G0,
  input  G1,
  input  G2,
  input  G3,
  input  P0,
  input  P1,
  input  P2,
  input  P3,
  input  C0,
  output out_10
);

  wire nand_1_out, nand_2_out, nand_3_out, nand_4_out, nand_5_out, nand_6_out, nor_1_out, not_1_out,
       not_2_out, not_3_out, not_4_out, not_5_out, not_6_out;

  not not_1 (not_1_out, G0);
  not not_2 (not_2_out, G2);
  not not_3 (not_3_out, G3);
  not not_4 (not_4_out, P1);
  not not_5 (not_5_out, P3);
  not not_6 (not_6_out, P2);
  nand nand_1 (nand_1_out, P2, G1);
  nor nor_1 (nor_1_out, not_4_out, not_6_out, not_5_out);
  nand nand_2 (nand_2_out, P0, C0);
  nand nand_3 (nand_3_out, not_2_out, nand_1_out);
  nand nand_4 (nand_4_out, not_1_out, nand_2_out);
  nand nand_5 (nand_5_out, P3, nand_3_out);
  nand nand_6 (nand_6_out, nor_1_out, nand_4_out);
  nand nand_7 (out_10, nand_5_out, not_3_out, nand_6_out);

  // Notes on the sheet:
  //   1.0
  //   2.0
  //   2.0
  //   1.0
  //   3.0
  //   2.0
  //   3.0
  //   4.0
endmodule

module AOI21 (
  input  c,
  input  b,
  input  a,
  output out_4
);

  wire transistor_1_out, transistor_3_out;

  Transistor transistor_1 (.in(1'b1), .out(transistor_1_out), .gate(c));
  Transistor #(.\type ("n")) transistor_2 (.in(transistor_3_out), .out(out_4), .gate(c));
  Transistor #(.\type ("n")) transistor_3 (.in(1'b0), .out(transistor_3_out), .gate(b));
  Transistor transistor_4 (.in(1'b1), .out(transistor_1_out), .gate(b));
  Transistor transistor_5 (.in(transistor_1_out), .out(out_4), .gate(a));
  Transistor #(.\type ("n")) transistor_6 (.in(1'b0), .out(out_4), .gate(a));
endmodule

module CLAC43 (
  input  G0,
  input  G1,
  input  G2,
  input  G3,
  input  P0,
  input  P1,
  input  P2,
  input  P3,
  input  C0,
  output out_10
);

  wire and_1_out, aoi21_1_out_4, aoi21_2_out_4, nand_1_out, nand_2_out, nand_3_out, nand_4_out, nand_5_out,
       nor_1_out, not_1_out, not_2_out;

  not not_1 (not_1_out, G3);
  and and_1 (and_1_out, P3, P1, P2);
  nand nand_1 (nand_1_out, P3, P2);
  nand nand_2 (nand_2_out, P1, P0);
  nand nand_3 (nand_3_out, P3, G1, P2);
  nand nand_4 (nand_4_out, P3, G2);
  nor nor_1 (nor_1_out, nand_1_out, nand_2_out);
  nand nand_5 (nand_5_out, nand_3_out, not_1_out, nand_4_out);
  not not_2 (not_2_out, aoi21_1_out_4);
  AOI21 aoi21_1 (.c(G0), .b(and_1_out), .a(nand_5_out), .out_4(aoi21_1_out_4));
  AOI21 aoi21_2 (.c(C0), .b(nor_1_out), .a(not_2_out), .out_4(aoi21_2_out_4));
  not not_3 (out_10, aoi21_2_out_4);

  // Notes on the sheet:
  //   1.25
  //   2.5
  //   3.75
  //   worst delay is 6.5
  //   4.5
  //   5.75
  //   c0 to c4 takes 1.25 through the aoi21, and then 0.75 through the inverter, so it takes 2.
  //   6.5
endmodule

module SubtractionOverflow (
  input  OP,
  input  [15:0] A,
  input  [15:0] B,
  output [15:0] out_4,
  output out_5
);

  wire and_1_out, and_2_out, not_1_out, not_2_out, not_4_out;
  wire [15:0] multiplexer_1_out, not_3_out;

  not not_1 (not_1_out, multiplexer_1_out[15]);
  not not_2 (not_2_out, A[15]);
  Multiplexer #(.width(16)) multiplexer_1 (.in0(B), .in1(not_3_out), .out(multiplexer_1_out), .sel(OP));
  assign not_3_out = ~B;  // NOT_Gate not_3, 16 bits wide
  SixteenBitCarryPart2 sixteenbitcarrypart2_1 (.b(multiplexer_1_out), .a(A), .in_2(OP), .out_4(out_4));  // open: _13
  not not_4 (not_4_out, out_4[15]);
  and and_1 (and_1_out, not_4_out, multiplexer_1_out[15], A[15]);
  and and_2 (and_2_out, out_4[15], not_1_out, not_2_out);
  or or_1 (out_5, and_1_out, and_2_out);
endmodule

module SixteenBitCarryPart2 (
  input  [15:0] a,
  input  in_2,
  input  [15:0] b,
  output [15:0] out_4,
  output _13
);

  wire eightbitcarryselectadder0_1_cout, eightbitcarryselectadder1_1_cout, eightbitcarryselectadder2_1_out_5,
       mx2i_1_x1;
  wire [7:0] eightbitcarryselectadder0_1__10_5, eightbitcarryselectadder1_1__10_5, mx2i_8_1_out_4;

  mx2i mx2i_1 (
    .sel(eightbitcarryselectadder2_1_out_5), .in0(eightbitcarryselectadder0_1_cout),
    .in1(eightbitcarryselectadder1_1_cout), .x1(mx2i_1_x1));
  not not_1 (_13, mx2i_1_x1);
  EightBitCarrySelectAdder1 eightbitcarryselectadder1_1 (
    .b(b[15:8]), .a(a[15:8]), .cout(eightbitcarryselectadder1_1_cout),
    ._10_5(eightbitcarryselectadder1_1__10_5));
  mx2i_8 mx2i_8_1 (
    .in_2(eightbitcarryselectadder1_1__10_5), .s(eightbitcarryselectadder2_1_out_5),
    .in_1(eightbitcarryselectadder0_1__10_5), .out_4(mx2i_8_1_out_4));
  EightBitCarrySelectAdder0 eightbitcarryselectadder0_1 (
    .b(b[15:8]), .a(a[15:8]), .cout(eightbitcarryselectadder0_1_cout),
    ._10_5(eightbitcarryselectadder0_1__10_5));
  assign out_4[15:8] = ~mx2i_8_1_out_4;  // NOT_Gate not_2, 8 bits wide
  EightBitCarrySelectAdder2 eightbitcarryselectadder2_1 (
    .b(b[7:0]), .a(a[7:0]), .in_2(in_2), .out_5(eightbitcarryselectadder2_1_out_5), ._10_5(out_4[7:0]));

  // Notes on the sheet:
  //   12.25
  //   10.5
  //   10.5
  //   10.5
  //   10.5
  //   12.25
  //   10.5
  //   10.5
  //   13
endmodule

module FourBitRippleCarryAdder1 (
  input  OP,
  input  [3:0] a,
  input  [3:0] b,
  output [3:0] _8_75,
  output _8
);

  wire faopt1_2_cout, faopt1_3_cout, faopt2_1_cout;

  FAopt1 faopt1_1 (.A(a[3]), .B(b[3]), .Cin(faopt1_2_cout), .Cout(_8), .S(_8_75[3]));
  FAopt1 faopt1_2 (.A(a[2]), .B(b[2]), .Cin(faopt2_1_cout), .Cout(faopt1_2_cout), .S(_8_75[2]));
  FAOpt2 faopt2_1 (.A(a[1]), .B(b[1]), .Cin(faopt1_3_cout), .Cout(faopt2_1_cout), .S(_8_75[1]));
  FAopt1 faopt1_3 (.A(a[0]), .B(b[0]), .Cin(OP), .Cout(faopt1_3_cout), .S(_8_75[0]));

  // Notes on the sheet:
  //   0
  //   0
  //   8
  //   8.75
  //   120 transistors
  //   6
  //   6.75
  //   4
  //   5.5
  //   cout
  //   1.75
  //   2.75
endmodule

module EightBitCarrySelectAdder2 (
  input  [7:0] a,
  input  in_2,
  input  [7:0] b,
  output [7:0] _10_5,
  output out_5
);

  wire fourbitripplecarry1_1__8, fourbitripplecarryadder0_1__8, fourbitripplecarryadder1_1__8, mx2i_1_x1;
  wire [3:0] fourbitripplecarry1_1__8_75, fourbitripplecarryadder0_1__8_75, mx2i_4_1_zb_3_0;

  mx2i mx2i_1 (
    .sel(fourbitripplecarryadder1_1__8), .in0(fourbitripplecarryadder0_1__8), .in1(fourbitripplecarry1_1__8),
    .x1(mx2i_1_x1));
  not not_1 (out_5, mx2i_1_x1);
  mx2i_4 mx2i_4_1 (
    .s(fourbitripplecarryadder1_1__8), .in_2(fourbitripplecarry1_1__8_75),
    .in_1(fourbitripplecarryadder0_1__8_75), .zb_3_0(mx2i_4_1_zb_3_0));
  assign _10_5[7:4] = ~mx2i_4_1_zb_3_0;  // NOT_Gate not_2, 4 bits wide
  FourBitRippleCarryAdder0 fourbitripplecarryadder0_1 (
    .a(a[7:4]), .b(b[7:4]), ._8(fourbitripplecarryadder0_1__8), ._8_75(fourbitripplecarryadder0_1__8_75));
  FourBitRippleCarry1 fourbitripplecarry1_1 (
    .a(a[7:4]), .b(b[7:4]), ._8(fourbitripplecarry1_1__8), ._8_75(fourbitripplecarry1_1__8_75));
  FourBitRippleCarryAdder1 fourbitripplecarryadder1_1 (
    .a(b[3:0]), .b(a[3:0]), .OP(in_2), ._8(fourbitripplecarryadder1_1__8), ._8_75(_10_5[3:0]));

  // Notes on the sheet:
  //   8
  //   8.75
  //   9.75
  //   8
  //   8.75
  //   9.75
  //   8
  //   8.75
  //   sum
endmodule

module Overflow3rdBit (
  input  OP,
  input  [3:0] A,
  input  [3:0] B,
  input  [3:0] R,
  output out_5
);

  wire and_1_out, and_2_out, not_1_out, not_2_out, not_4_out;
  wire [3:0] multiplexer_1_out, not_3_out;

  not not_1 (not_1_out, multiplexer_1_out[3]);
  not not_2 (not_2_out, A[3]);
  Multiplexer #(.width(4)) multiplexer_1 (.in0(B), .in1(not_3_out), .out(multiplexer_1_out), .sel(OP));
  assign not_3_out = ~B;  // NOT_Gate not_3, 4 bits wide
  not not_4 (not_4_out, R[3]);
  and and_1 (and_1_out, not_4_out, multiplexer_1_out[3], A[3]);
  and and_2 (and_2_out, R[3], not_1_out, not_2_out);
  or or_1 (out_5, and_1_out, and_2_out);
endmodule

module R0R1Registers (
  input  in_1,
  input  subtract,
  input  [15:0] in_3
);

  wire clk;
  wire [15:0] R0, R1, subtractionoverflow_1_out_4;

  Clock clock_1 (.out(clk));
  Register #(.width(16)) u_R0 (.D(subtractionoverflow_1_out_4), .en(1'b1), .clk(clk), .Q(R0), .clr(in_1));
  Register #(.width(16)) u_R1 (.D(in_3), .en(1'b1), .clk(clk), .Q(R1), .clr(in_1));
  Hex_Digit_Display hex_digit_display_1 (.value(R0[15:12]));  // open: dp
  Hex_Digit_Display hex_digit_display_2 (.value(R0[11:8]));  // open: dp
  SubtractionOverflow subtractionoverflow_1 (
    .A(R0), .OP(subtract), .B(R1), .out_4(subtractionoverflow_1_out_4));  // open: out_5
  Hex_Digit_Display hex_digit_display_3 (.value(R0[7:4]));  // open: dp
  Hex_Digit_Display hex_digit_display_4 (.value(R0[3:0]));  // open: dp
  Hex_Digit_Display hex_digit_display_5 (.value(R1[15:12]));  // open: dp
  Hex_Digit_Display hex_digit_display_6 (.value(R1[11:8]));  // open: dp
  Hex_Digit_Display hex_digit_display_7 (.value(R1[7:4]));  // open: dp
  Hex_Digit_Display hex_digit_display_8 (.value(R1[3:0]));  // open: dp

  // Other names for the same wires on the sheet: rst = in_1
endmodule

module R2R3Registers (
  input  in_1
);

  wire clk, not_1_out, not_2_out, ovrfl, reg0WE, reg1WE, reg2WE, reg3WE, register_1_q, subtrac;
  wire [1:0] Rd, Rs;
  wire [3:0] ram_1_dout;
  wire [5:0] programcounter_1_pc;
  wire [15:0] A, B, R0, R1, R2, R3, subtractionoverflow_1_out_4;

  Clock clock_1 (.out(clk));
  Register #(.width(16)) u_R0 (.D(subtractionoverflow_1_out_4), .en(reg0WE), .clk(clk), .Q(R0), .clr(in_1));
  Register #(.width(16)) u_R1 (.D(subtractionoverflow_1_out_4), .en(reg1WE), .clk(clk), .Q(R1), .clr(in_1));
  Register #(.width(16)) u_R2 (.D(subtractionoverflow_1_out_4), .en(reg2WE), .clk(clk), .Q(R2), .clr(in_1));
  Register #(.width(16)) u_R3 (.D(subtractionoverflow_1_out_4), .en(reg3WE), .clk(clk), .Q(R3), .clr(in_1));
  Hex_Digit_Display hex_digit_display_1 (.value(R2[15:12]));  // open: dp
  Hex_Digit_Display hex_digit_display_2 (.value(R0[15:12]));  // open: dp
  Hex_Digit_Display hex_digit_display_3 (.value(R0[11:8]));  // open: dp
  Hex_Digit_Display hex_digit_display_4 (.value(R2[11:8]));  // open: dp
  SubtractionOverflow subtractionoverflow_1 (
    .A(A), .OP(subtrac), .B(B), .out_4(subtractionoverflow_1_out_4), .out_5(ovrfl));
  Hex_Digit_Display hex_digit_display_5 (.value(R0[7:4]));  // open: dp
  Hex_Digit_Display hex_digit_display_6 (.value(R2[7:4]));  // open: dp
  Hex_Digit_Display hex_digit_display_7 (.value(R2[3:0]));  // open: dp
  Hex_Digit_Display hex_digit_display_8 (.value(R0[3:0]));  // open: dp
  Hex_Digit_Display hex_digit_display_9 (.value(R3[15:12]));  // open: dp
  Hex_Digit_Display hex_digit_display_10 (.value(R1[15:12]));  // open: dp
  Hex_Digit_Display hex_digit_display_11 (.value(R1[11:8]));  // open: dp
  Hex_Digit_Display hex_digit_display_12 (.value(R3[11:8]));  // open: dp
  Hex_Digit_Display hex_digit_display_13 (.value(R1[7:4]));  // open: dp
  Hex_Digit_Display hex_digit_display_14 (.value(R3[7:4]));  // open: dp
  Hex_Digit_Display hex_digit_display_15 (.value(R3[3:0]));  // open: dp
  WriteEnableRegisters writeenableregisters_1 (
    .Rd(Rd), .regWrite(1'b1), .reg0WE(reg0WE), .reg1WE(reg1WE), .reg2WE(reg2WE), .reg3WE(reg3WE));
  Hex_Digit_Display hex_digit_display_16 (.value(R1[3:0]));  // open: dp
  Register #(.width(1)) register_1 (.D(1'b1), .en(ovrfl), .clk(clk), .Q(register_1_q), .clr(in_1));
  LED led_1 (.in(register_1_q));
  srcSel srcsel_1 (.sel(Rd), .reg0(R0), .reg1(R1), .reg2(R2), .reg3(R3), .out_6(A));
  srcSel srcsel_2 (.sel(Rs), .reg0(R0), .reg1(R1), .reg2(R2), .reg3(R3), .out_6(B));
  RAM #(.addrWidth(6), .enables("line"), .trigger("falling")) ram_1 (
    .addr(programcounter_1_pc), .we(1'b0), .oe(1'b1), .clk(clk), .dout({Rd, Rs, ram_1_dout}));  // open: din
  programCounter programcounter_1 (.clk(clk), .rst(in_1), .pc(programcounter_1_pc));  // open: jumpaddress, jump, jumpn
  not not_1 (not_1_out, ram_1_dout[2]);
  not not_2 (not_2_out, ram_1_dout[3]);
  and and_1 (subtrac, ram_1_dout[0], ram_1_dout[1], not_1_out, not_2_out);

  // Other names for the same wires on the sheet: rst = in_1

  // Notes on the sheet:
  //   5341
  //   537d
  //   4c41
  //   7b43
  //   b3 43 e2 32 82
endmodule

module WriteEnableRegisters (
  input  [1:0] Rd,
  input  regWrite,
  output reg0WE,
  output reg1WE,
  output reg2WE,
  output reg3WE
);

  wire not_1_out, not_2_out, not_3_out;

  not not_1 (not_1_out, regWrite);
  not not_2 (not_2_out, Rd[1]);
  not not_3 (not_3_out, Rd[0]);
  nor nor_1 (reg0WE, Rd[0], Rd[1], not_1_out);
  and and_1 (reg1WE, Rd[0], not_2_out, regWrite);
  and and_2 (reg2WE, not_3_out, Rd[1], regWrite);
  and and_3 (reg3WE, Rd[0], Rd[1], regWrite);
endmodule

module srcSel (
  input  [1:0] sel,
  input  [15:0] reg0,
  input  [15:0] reg1,
  input  [15:0] reg2,
  input  [15:0] reg3,
  output [15:0] out_6
);

  Multiplexer #(.select(2), .width(16)) multiplexer_1 (
    .in0(reg0), .in1(reg1), .in2(reg2), .in3(reg3), .out(out_6), .sel(sel));
endmodule

module programCounter (
  input  clk,
  input  rst,
  input  [5:0] jumpaddress,
  input  jump,
  input  jumpn,
  output [5:0] pc
);

  wire or_1_out;
  wire [5:0] adder_1_out, multiplexer_1_out;

  Multiplexer #(.width(6)) multiplexer_1 (
    .in0(adder_1_out), .in1(jumpaddress), .out(multiplexer_1_out), .sel(or_1_out));
  Register #(.width(6)) R0 (.D(multiplexer_1_out), .en(1'b1), .clk(clk), .Q(pc), .clr(rst));
  or or_1 (or_1_out, jumpn, jump);
  Adder #(.width(6)) adder_1 (.a(pc), .b(6'b000001), .out(adder_1_out));  // open: cin, cout
endmodule

module R2R3RegistersAgain (
  input  in_1
);

  wire clk, d_ff_1_q, d_ff_2_q, ovrfl, reg0WE, reg1WE, reg2WE, reg3WE, register_1_q, subtrac;
  wire [1:0] Rd, Rs;
  wire [5:0] programcounter_1_pc;
  wire [7:0] ram_1_dout, register_2_q;
  wire [15:0] A, B, R0, R1, R2, R3, subtractionoverflow_1_out_4;

  Clock clock_1 (.out(clk));
  Register #(.width(16)) u_R0 (.D(subtractionoverflow_1_out_4), .en(reg0WE), .clk(clk), .Q(R0), .clr(in_1));
  Register #(.width(16)) u_R1 (.D(subtractionoverflow_1_out_4), .en(reg1WE), .clk(clk), .Q(R1), .clr(in_1));
  Register #(.width(16)) u_R2 (.D(subtractionoverflow_1_out_4), .en(reg2WE), .clk(clk), .Q(R2), .clr(in_1));
  Register #(.width(16)) u_R3 (.D(subtractionoverflow_1_out_4), .en(reg3WE), .clk(clk), .Q(R3), .clr(in_1));
  Hex_Digit_Display hex_digit_display_1 (.value(R0[15:12]));  // open: dp
  Hex_Digit_Display hex_digit_display_2 (.value(R0[11:8]));  // open: dp
  Hex_Digit_Display hex_digit_display_3 (.value(R2[15:12]));  // open: dp
  Hex_Digit_Display hex_digit_display_4 (.value(R2[11:8]));  // open: dp
  SubtractionOverflow subtractionoverflow_1 (
    .A(A), .OP(subtrac), .B(B), .out_4(subtractionoverflow_1_out_4), .out_5(ovrfl));
  Hex_Digit_Display hex_digit_display_5 (.value(R0[7:4]));  // open: dp
  Hex_Digit_Display hex_digit_display_6 (.value(R2[7:4]));  // open: dp
  D_Flip_Flop d_ff_1 (.D(1'b1), .clk(clk), .Q(d_ff_1_q), .reset(in_1));  // open: Qn, preset
  Hex_Digit_Display hex_digit_display_7 (.value(R0[3:0]));  // open: dp
  Hex_Digit_Display hex_digit_display_8 (.value(R2[3:0]));  // open: dp
  Hex_Digit_Display hex_digit_display_9 (.value(R1[15:12]));  // open: dp
  Hex_Digit_Display hex_digit_display_10 (.value(R1[11:8]));  // open: dp
  Hex_Digit_Display hex_digit_display_11 (.value(R3[15:12]));  // open: dp
  Hex_Digit_Display hex_digit_display_12 (.value(R3[11:8]));  // open: dp
  D_Flip_Flop d_ff_2 (.D(d_ff_1_q), .clk(clk), .Q(d_ff_2_q), .reset(in_1));  // open: Qn, preset
  Hex_Digit_Display hex_digit_display_13 (.value(R1[7:4]));  // open: dp
  Hex_Digit_Display hex_digit_display_14 (.value(R3[7:4]));  // open: dp
  WriteEnableRegisters writeenableregisters_1 (
    .Rd(Rd), .regWrite(d_ff_2_q), .reg0WE(reg0WE), .reg1WE(reg1WE), .reg2WE(reg2WE), .reg3WE(reg3WE));
  Hex_Digit_Display hex_digit_display_15 (.value(R1[3:0]));  // open: dp
  Hex_Digit_Display hex_digit_display_16 (.value(R3[3:0]));  // open: dp
  Register #(.width(1)) register_1 (.D(d_ff_2_q), .en(ovrfl), .clk(clk), .Q(register_1_q), .clr(in_1));
  LED led_1 (.in(register_1_q));
  srcSel srcsel_1 (.sel(Rd), .reg0(R0), .reg1(R1), .reg2(R2), .reg3(R3), .out_6(A));
  srcSel srcsel_2 (.sel(Rs), .reg0(R0), .reg1(R1), .reg2(R2), .reg3(R3), .out_6(B));
  programCounter programcounter_1 (.clk(clk), .rst(in_1), .pc(programcounter_1_pc));  // open: jumpaddress, jump, jumpn
  RAM #(.addrWidth(6), .enables("line"), .trigger("falling")) ram_1 (
    .addr(programcounter_1_pc), .we(1'b0), .clk(clk), .dout(ram_1_dout));  // open: din
  Register register_2 (.D(ram_1_dout), .en(1'b1), .clk(clk), .Q(register_2_q), .clr(in_1));
  IRDecoder irdecoder_1 (.IR(register_2_q), .clk(clk), .rst(in_1), .sub(subtrac), .Rs(Rs), .Rd(Rd));

  // Other names for the same wires on the sheet: rst = in_1

  // Notes on the sheet:
  //   5341
  //   537d
  //   4c41
  //   7b43
  //   b3 43 e2 32 82
endmodule

module IRDecoder (
  input  [7:0] IR,
  input  clk,
  input  rst,
  output sub,
  output [1:0] Rs,
  output [1:0] Rd
);

  wire and_1_out, not_1_out, not_2_out;

  not not_1 (not_1_out, IR[2]);
  not not_2 (not_2_out, IR[3]);
  and and_1 (and_1_out, IR[0], IR[1], not_1_out, not_2_out);
  D_Flip_Flop d_ff_1 (.D(and_1_out), .clk(clk), .Q(sub), .reset(rst));  // open: Qn, preset
  Register #(.width(2)) register_1 (.D(IR[5:4]), .en(1'b1), .clk(clk), .Q(Rs), .clr(rst));
  Register #(.width(2)) register_2 (.D(IR[7:6]), .en(1'b1), .clk(clk), .Q(Rd), .clr(rst));
endmodule

module LoadingData (
  input  in_1,
  output [15:0] out_2
);

  wire clk, d_ff_1_q, d_ff_2_q, id, idi, ovrfl, reg0WE, reg1WE, reg2WE, reg3WE, register_1_q, subtrac;
  wire [1:0] Rd;
  wire [5:0] programcounter_1_pc;
  wire [7:0] InstructionRegister_q, ram_1_dout;
  wire [15:0] A, B, data, DataRAM_dout, multiplexer_1_out, putput, R0, R1, R2, R3;

  Clock clock_1 (.out(clk));
  Register #(.width(16)) u_R0 (.D(putput), .en(reg0WE), .clk(clk), .Q(R0), .clr(in_1));
  Register #(.width(16)) u_R1 (.D(putput), .en(reg1WE), .clk(clk), .Q(R1), .clr(in_1));
  Register #(.width(16)) u_R2 (.D(putput), .en(reg2WE), .clk(clk), .Q(R2), .clr(in_1));
  Register #(.width(16)) u_R3 (.D(putput), .en(reg3WE), .clk(clk), .Q(R3), .clr(in_1));
  Hex_Digit_Display hex_digit_display_1 (.value(R0[15:12]));  // open: dp
  Hex_Digit_Display hex_digit_display_2 (.value(R0[11:8]));  // open: dp
  Hex_Digit_Display hex_digit_display_3 (.value(R2[15:12]));  // open: dp
  Hex_Digit_Display hex_digit_display_4 (.value(R2[11:8]));  // open: dp
  SubtractionOverflow subtractionoverflow_1 (.A(A), .OP(subtrac), .B(B), .out_4(data), .out_5(ovrfl));
  Hex_Digit_Display hex_digit_display_5 (.value(R0[7:4]));  // open: dp
  Hex_Digit_Display hex_digit_display_6 (.value(R2[7:4]));  // open: dp
  D_Flip_Flop d_ff_1 (.D(1'b1), .clk(clk), .Q(d_ff_1_q), .reset(in_1));  // open: Qn, preset
  Hex_Digit_Display hex_digit_display_7 (.value(R0[3:0]));  // open: dp
  Hex_Digit_Display hex_digit_display_8 (.value(R2[3:0]));  // open: dp
  Hex_Digit_Display hex_digit_display_9 (.value(R1[15:12]));  // open: dp
  Hex_Digit_Display hex_digit_display_10 (.value(R1[11:8]));  // open: dp
  Hex_Digit_Display hex_digit_display_11 (.value(R3[15:12]));  // open: dp
  Hex_Digit_Display hex_digit_display_12 (.value(R3[11:8]));  // open: dp
  D_Flip_Flop d_ff_2 (.D(d_ff_1_q), .clk(clk), .Q(d_ff_2_q), .reset(in_1));  // open: Qn, preset
  Hex_Digit_Display hex_digit_display_13 (.value(R1[7:4]));  // open: dp
  Hex_Digit_Display hex_digit_display_14 (.value(R3[7:4]));  // open: dp
  WriteEnableRegisters writeenableregisters_1 (
    .Rd(Rd), .regWrite(d_ff_2_q), .reg0WE(reg0WE), .reg1WE(reg1WE), .reg2WE(reg2WE), .reg3WE(reg3WE));
  Hex_Digit_Display hex_digit_display_15 (.value(R1[3:0]));  // open: dp
  Hex_Digit_Display hex_digit_display_16 (.value(R3[3:0]));  // open: dp
  Register #(.width(1)) register_1 (.D(d_ff_2_q), .en(ovrfl), .clk(clk), .Q(register_1_q), .clr(in_1));
  LED led_1 (.in(register_1_q));
  srcSel srcsel_1 (.sel(Rd), .reg0(R0), .reg1(R1), .reg2(R2), .reg3(R3), .out_6(A));
  srcSel srcsel_2 (.sel(out_2[1:0]), .reg0(R0), .reg1(R1), .reg2(R2), .reg3(R3), .out_6(B));
  programCounter programcounter_1 (.clk(clk), .rst(in_1), .pc(programcounter_1_pc));  // open: jumpaddress, jump, jumpn
  RAM #(.addrWidth(4), .asyncread("true"), .dataWidth(16), .trigger("falling")) DataRAM (
    .addr(B[3:0]), .we(1'b0), .oe(clk), .clk(clk), .dout(DataRAM_dout));  // open: din
  RAM #(.addrWidth(6), .asyncread("true"), .trigger("falling")) ram_1 (
    .addr(programcounter_1_pc), .we(1'b0), .oe(1'b1), .clk(clk), .dout(ram_1_dout));  // open: din
  Register InstructionRegister (.D(ram_1_dout), .en(1'b1), .clk(clk), .Q(InstructionRegister_q), .clr(in_1));
  Multiplexer #(.width(16)) multiplexer_1 (.in0(data), .in1(DataRAM_dout), .out(multiplexer_1_out), .sel(id));
  Multiplexer #(.width(16)) multiplexer_2 (
    .in0(multiplexer_1_out), .in1({{14{1'b0}}, out_2[1:0]}), .out(putput), .sel(idi));
  IRDecoder2 irdecoder2_1 (
    .clk(clk), .rst(in_1), .IR(InstructionRegister_q), .Id(id), .Idi(idi), .sub(subtrac), .Rs(out_2[1:0]),
    .Rd(Rd));

  assign out_2[15:2] = {14{1'b0}};

  // Other names for the same wires on the sheet: Rs[1:0] = out_2[1:0]; rst = in_1

  // Notes on the sheet:
  //   5341
  //   537d
  //   number is put here and is added to R1 and stored back in here
  //   can be used to access
  //   4c41
  //   7b43
  //   add
  //   subtract
  //   b3 43 e2 32 82
endmodule

module IRDecoder2 (
  input  clk,
  input  rst,
  input  [7:0] IR,
  output Id,
  output Idi,
  output sub,
  output [1:0] Rs,
  output [1:0] Rd
);

  wire and_1_out, and_2_out, and_3_out, not_1_out, not_2_out, not_3_out;

  not not_1 (not_1_out, IR[0]);
  not not_2 (not_2_out, IR[2]);
  not not_3 (not_3_out, IR[3]);
  and and_1 (and_1_out, not_1_out, IR[1], IR[2], IR[3]);
  and and_2 (and_2_out, IR[0], IR[1], not_2_out, not_3_out);
  D_Flip_Flop d_ff_1 (.D(and_2_out), .clk(clk), .Q(sub), .reset(rst));  // open: Qn, preset
  and and_3 (and_3_out, IR[0], IR[1], IR[2], IR[3]);
  D_Flip_Flop d_ff_2 (.D(and_1_out), .clk(clk), .Q(Idi), .reset(rst));  // open: Qn, preset
  Register #(.width(2)) register_1 (.D(IR[5:4]), .en(1'b1), .clk(clk), .Q(Rs), .clr(rst));
  Register #(.width(2)) register_2 (.D(IR[7:6]), .en(1'b1), .clk(clk), .Q(Rd), .clr(rst));
  D_Flip_Flop d_ff_3 (.D(and_3_out), .clk(clk), .Q(Id), .reset(rst));  // open: Qn, preset
endmodule

module LoadingDataDebug (
  input  in_1,
  output [15:0] out_2
);

  wire clk, d_ff_1_q, d_ff_2_q, ld, ldi, ovrfl, reg0WE, reg1WE, reg2WE, reg3WE, register_1_q, subtrac;
  wire [1:0] Rd;
  wire [5:0] programcounter_1_pc;
  wire [7:0] InstructionRegister_q, ram_1_dout;
  wire [15:0] A, B, DataRAM_dout, multiplexer_1_out, mux2, output1, R0, R1, R2, R3;

  Clock clock_1 (.out(clk));
  Register #(.width(16)) u_R0 (.D(output1), .en(reg0WE), .clk(clk), .Q(R0), .clr(in_1));
  Register #(.width(16)) u_R1 (.D(output1), .en(reg1WE), .clk(clk), .Q(R1), .clr(in_1));
  Register #(.width(16)) u_R2 (.D(output1), .en(reg2WE), .clk(clk), .Q(R2), .clr(in_1));
  Register #(.width(16)) u_R3 (.D(output1), .en(reg3WE), .clk(clk), .Q(R3), .clr(in_1));
  Hex_Digit_Display hex_digit_display_1 (.value(R0[15:12]));  // open: dp
  Hex_Digit_Display hex_digit_display_2 (.value(R0[11:8]));  // open: dp
  Hex_Digit_Display hex_digit_display_3 (.value(R2[15:12]));  // open: dp
  Hex_Digit_Display hex_digit_display_4 (.value(R2[11:8]));  // open: dp
  SubtractionOverflow subtractionoverflow_1 (.A(A), .OP(subtrac), .B(B), .out_4(mux2), .out_5(ovrfl));
  Hex_Digit_Display hex_digit_display_5 (.value(R0[7:4]));  // open: dp
  Hex_Digit_Display hex_digit_display_6 (.value(R2[7:4]));  // open: dp
  D_Flip_Flop d_ff_1 (.D(1'b1), .clk(clk), .Q(d_ff_1_q), .reset(in_1));  // open: Qn, preset
  Hex_Digit_Display hex_digit_display_7 (.value(R0[3:0]));  // open: dp
  Hex_Digit_Display hex_digit_display_8 (.value(R2[3:0]));  // open: dp
  Hex_Digit_Display hex_digit_display_9 (.value(R1[15:12]));  // open: dp
  Hex_Digit_Display hex_digit_display_10 (.value(R1[11:8]));  // open: dp
  Hex_Digit_Display hex_digit_display_11 (.value(R3[15:12]));  // open: dp
  Hex_Digit_Display hex_digit_display_12 (.value(R3[11:8]));  // open: dp
  D_Flip_Flop d_ff_2 (.D(d_ff_1_q), .clk(clk), .Q(d_ff_2_q), .reset(in_1));  // open: Qn, preset
  Hex_Digit_Display hex_digit_display_13 (.value(R1[7:4]));  // open: dp
  Hex_Digit_Display hex_digit_display_14 (.value(R3[7:4]));  // open: dp
  WriteEnableRegisters writeenableregisters_1 (
    .Rd(Rd), .regWrite(d_ff_2_q), .reg0WE(reg0WE), .reg1WE(reg1WE), .reg2WE(reg2WE), .reg3WE(reg3WE));
  Hex_Digit_Display hex_digit_display_15 (.value(R1[3:0]));  // open: dp
  Hex_Digit_Display hex_digit_display_16 (.value(R3[3:0]));  // open: dp
  Register #(.width(1)) register_1 (.D(d_ff_2_q), .en(ovrfl), .clk(clk), .Q(register_1_q));  // open: clr
  LED led_1 (.in(register_1_q));
  srcSel srcsel_1 (.sel(Rd), .reg0(R0), .reg1(R1), .reg2(R2), .reg3(R3), .out_6(A));
  srcSel srcsel_2 (.sel(out_2[1:0]), .reg0(R0), .reg1(R1), .reg2(R2), .reg3(R3), .out_6(B));
  RAM #(.addrWidth(4), .asyncread("true"), .dataWidth(16), .trigger("falling")) DataRAM (
    .addr(B[3:0]), .we(1'b0), .oe(clk), .clk(clk), .dout(DataRAM_dout));  // open: din
  programCounter programcounter_1 (.clk(clk), .rst(in_1), .pc(programcounter_1_pc));  // open: jumpaddress, jump, jumpn
  Multiplexer #(.width(16)) multiplexer_1 (.in0(mux2), .in1(DataRAM_dout), .out(multiplexer_1_out), .sel(ld));
  Multiplexer #(.width(16)) multiplexer_2 (
    .in0(multiplexer_1_out), .in1({{14{1'b0}}, out_2[1:0]}), .out(output1), .sel(ldi));
  RAM #(.addrWidth(6), .asyncread("true"), .trigger("falling")) ram_1 (
    .addr(programcounter_1_pc), .we(1'b0), .oe(1'b1), .clk(clk), .dout(ram_1_dout));  // open: din
  Register InstructionRegister (.D(ram_1_dout), .en(1'b1), .clk(clk), .Q(InstructionRegister_q), .clr(in_1));
  IRDecoder2 irdecoder2_1 (
    .clk(clk), .rst(in_1), .IR(InstructionRegister_q), .Id(ld), .Idi(ldi), .sub(subtrac), .Rs(out_2[1:0]),
    .Rd(Rd));

  assign out_2[15:2] = {14{1'b0}};

  // Other names for the same wires on the sheet: Rs[1:0] = out_2[1:0]; rst = in_1

  // Notes on the sheet:
  //   5341
  //   537d
  //   can be used to access
  //   4c41
  //   7b43
  //   loadimmediate
  //   add
  //   subtract
  //   b3 43 e2 32 82
endmodule

module Fibonacci (
  input  in_1,
  output [15:0] out_2
);

  wire clk, d_ff_1_q, d_ff_2_q, id, idi, move, ovrfl, reg0WE, reg1WE, reg2WE, reg3WE, register_1_q, regwrite,
       store, subtrac;
  wire [1:0] Rd;
  wire [5:0] programcounter_1_pc;
  wire [7:0] InstructionRegister_q, ram_1_dout;
  wire [15:0] A, B, data, DataRAM_dout, multiplexer_2_out, multiplexer_3_out, putput, R0, R1, R2, R3;

  Register #(.width(16)) u_R0 (.D(putput), .en(reg0WE), .clk(clk), .Q(R0), .clr(in_1));
  Register #(.width(16)) u_R1 (.D(putput), .en(reg1WE), .clk(clk), .Q(R1), .clr(in_1));
  Register #(.width(16)) u_R2 (.D(putput), .en(reg2WE), .clk(clk), .Q(R2), .clr(in_1));
  Register #(.width(16)) u_R3 (.D(putput), .en(reg3WE), .clk(clk), .Q(R3), .clr(in_1));
  Clock clock_1 (.out(clk));
  Hex_Digit_Display hex_digit_display_1 (.value(R0[15:12]));  // open: dp
  Hex_Digit_Display hex_digit_display_2 (.value(R0[11:8]));  // open: dp
  Hex_Digit_Display hex_digit_display_3 (.value(R2[15:12]));  // open: dp
  Hex_Digit_Display hex_digit_display_4 (.value(R2[11:8]));  // open: dp
  SubtractionOverflow subtractionoverflow_1 (.A(A), .OP(subtrac), .B(B), .out_4(data), .out_5(ovrfl));
  Hex_Digit_Display hex_digit_display_5 (.value(R0[7:4]));  // open: dp
  Hex_Digit_Display hex_digit_display_6 (.value(R2[7:4]));  // open: dp
  Hex_Digit_Display hex_digit_display_7 (.value(R0[3:0]));  // open: dp
  Hex_Digit_Display hex_digit_display_8 (.value(R2[3:0]));  // open: dp
  Hex_Digit_Display hex_digit_display_9 (.value(R1[15:12]));  // open: dp
  Hex_Digit_Display hex_digit_display_10 (.value(R1[11:8]));  // open: dp
  Hex_Digit_Display hex_digit_display_11 (.value(R3[15:12]));  // open: dp
  Hex_Digit_Display hex_digit_display_12 (.value(R3[11:8]));  // open: dp
  Hex_Digit_Display hex_digit_display_13 (.value(R1[7:4]));  // open: dp
  Hex_Digit_Display hex_digit_display_14 (.value(R3[7:4]));  // open: dp
  WriteEnableRegisters writeenableregisters_1 (
    .Rd(Rd), .regWrite(regwrite), .reg0WE(reg0WE), .reg1WE(reg1WE), .reg2WE(reg2WE), .reg3WE(reg3WE));
  Hex_Digit_Display hex_digit_display_15 (.value(R1[3:0]));  // open: dp
  Hex_Digit_Display hex_digit_display_16 (.value(R3[3:0]));  // open: dp
  Register #(.width(1)) register_1 (.D(regwrite), .en(ovrfl), .clk(clk), .Q(register_1_q), .clr(in_1));
  D_Flip_Flop d_ff_1 (.D(1'b1), .clk(clk), .Q(d_ff_1_q), .reset(in_1));  // open: Qn, preset
  LED led_1 (.in(register_1_q));
  D_Flip_Flop d_ff_2 (.D(d_ff_1_q), .clk(clk), .Q(d_ff_2_q), .reset(in_1));  // open: Qn, preset
  srcSel srcsel_1 (.sel(Rd), .reg0(R0), .reg1(R1), .reg2(R2), .reg3(R3), .out_6(A));
  srcSel srcsel_2 (.sel(out_2[1:0]), .reg0(R0), .reg1(R1), .reg2(R2), .reg3(R3), .out_6(B));
  Multiplexer multiplexer_1 (.in0(d_ff_2_q), .in1(1'b0), .out(regwrite), .sel(store));
  programCounter programcounter_1 (.clk(clk), .rst(in_1), .pc(programcounter_1_pc));  // open: jumpaddress, jump, jumpn
  RAM #(.addrWidth(4), .asyncread("true"), .dataWidth(16), .trigger("falling")) DataRAM (
    .addr(B[3:0]), .we(store), .oe(1'b1), .clk(clk), .din(A), .dout(DataRAM_dout));
  RAM #(.addrWidth(6), .asyncread("true"), .trigger("falling")) ram_1 (
    .addr(programcounter_1_pc), .we(1'b0), .oe(1'b1), .clk(clk), .dout(ram_1_dout));  // open: din
  Register InstructionRegister (.D(ram_1_dout), .en(1'b1), .clk(clk), .Q(InstructionRegister_q), .clr(in_1));
  Multiplexer #(.width(16)) multiplexer_2 (.in0(data), .in1(DataRAM_dout), .out(multiplexer_2_out), .sel(id));
  Multiplexer #(.width(16)) multiplexer_3 (
    .in0(multiplexer_2_out), .in1({{14{1'b0}}, out_2[1:0]}), .out(multiplexer_3_out), .sel(idi));
  Multiplexer #(.width(16)) multiplexer_4 (.in0(multiplexer_3_out), .in1(B), .out(putput), .sel(move));
  IRDecoder3 irdecoder3_1 (
    .clk(clk), .rst(in_1), .IR(InstructionRegister_q), .store(store), .move(move), .Id(id), .Idi(idi),
    .sub(subtrac), .Rs(out_2[1:0]), .Rd(Rd));

  assign out_2[15:2] = {14{1'b0}};

  // Other names for the same wires on the sheet: Rs[1:0] = out_2[1:0]; rst = in_1

  // Notes on the sheet:
  //   5341
  //   537d
  //   number is put here
  //   can be used to access
  //   4c41
  //   7b43
  //   address comes after you click once more on the number you get, so once u get 59, click one more and u get the right address 9.
  //   add
  //   subtract
  //   b3 43 e2 32 82
endmodule

module IRDecoder3 (
  input  clk,
  input  rst,
  input  [7:0] IR,
  output store,
  output move,
  output Id,
  output Idi,
  output sub,
  output [1:0] Rs,
  output [1:0] Rd
);

  wire and_1_out, and_2_out, and_3_out, and_4_out, and_5_out, not_1_out, not_2_out, not_3_out, not_4_out,
       not_5_out;

  Register #(.width(2)) register_1 (.D(IR[7:6]), .en(1'b1), .clk(clk), .Q(Rd), .clr(rst));
  Register #(.width(2)) register_2 (.D(IR[5:4]), .en(1'b1), .clk(clk), .Q(Rs));  // open: clr
  and and_1 (and_1_out, IR[0], IR[1], not_2_out, IR[3]);
  not not_1 (not_1_out, IR[1]);
  not not_2 (not_2_out, IR[2]);
  not not_3 (not_3_out, IR[0]);
  not not_4 (not_4_out, IR[2]);
  not not_5 (not_5_out, IR[3]);
  D_Flip_Flop d_ff_1 (.D(and_1_out), .clk(clk), .Q(store), .reset(rst));  // open: Qn, preset
  D_Flip_Flop d_ff_2 (.D(and_2_out), .clk(clk), .Q(move), .reset(rst));  // open: Qn, preset
  and and_2 (and_2_out, IR[0], not_1_out, not_2_out, IR[3]);
  and and_3 (and_3_out, not_3_out, IR[1], IR[2], IR[3]);
  and and_4 (and_4_out, IR[0], IR[1], not_4_out, not_5_out);
  D_Flip_Flop d_ff_3 (.D(and_3_out), .clk(clk), .Q(Idi), .reset(rst));  // open: Qn, preset
  D_Flip_Flop d_ff_4 (.D(and_4_out), .clk(clk), .Q(sub), .reset(rst));  // open: Qn, preset
  and and_5 (and_5_out, IR[0], IR[1], IR[2], IR[3]);
  D_Flip_Flop d_ff_5 (.D(and_5_out), .clk(clk), .Q(Id), .reset(rst));  // open: Qn, preset

  // Other names for the same wires on the sheet: first = IR[0]; middle = IR[1]; middle2 = IR[2]; last = IR[3]

  // Notes on the sheet:
  //   move is incorrect but im too lazy to fix it on this decoder lmao
endmodule

module IRDecoder4 (
  input  clk,
  input  rst,
  input  [7:0] Ir,
  output [1:0] Rs,
  output [1:0] Rd,
  output subtrac,
  output ldi,
  output ld,
  output move,
  output store,
  output halt,
  output [5:0] jmpaddress,
  output jmp
);

  wire and_1_out, and_2_out, and_3_out, and_4_out, and_5_out, and_6_out, d_ff_7_q, d_ff_8_q, d_ff_9_q,
       nor_1_out, not_1_out, not_2_out, not_3_out, not_4_out, not_5_out, not_6_out, not_7_out, not_8_out;

  not not_1 (not_1_out, Ir[2]);
  not not_2 (not_2_out, Ir[3]);
  not not_3 (not_3_out, Ir[0]);
  not not_4 (not_4_out, Ir[0]);
  not not_5 (not_5_out, Ir[3]);
  not not_6 (not_6_out, Ir[2]);
  not not_7 (not_7_out, Ir[0]);
  Register #(.width(2)) register_1 (.D(Ir[7:6]), .en(1'b1), .clk(clk), .Q(Rd), .clr(rst));
  and and_1 (and_1_out, Ir[0], Ir[1], not_1_out, not_2_out);
  and and_2 (and_2_out, not_3_out, Ir[1], Ir[2], Ir[3]);
  not not_8 (not_8_out, Ir[3]);
  Register #(.width(6)) register_2 (.D(Ir[7:2]), .en(1'b1), .clk(clk), .Q(jmpaddress), .clr(rst));
  D_Flip_Flop d_ff_1 (.D(and_1_out), .clk(clk), .Q(subtrac), .reset(rst));  // open: Qn, preset
  D_Flip_Flop d_ff_2 (.D(and_2_out), .clk(clk), .Q(ldi), .reset(rst));  // open: Qn, preset
  D_Flip_Flop d_ff_3 (.D(and_3_out), .clk(clk), .Q(ld), .reset(rst));  // open: Qn, preset
  and and_3 (and_3_out, Ir[0], Ir[1], Ir[2], Ir[3]);
  and and_4 (and_4_out, not_4_out, Ir[1], Ir[2], not_5_out);
  and and_5 (and_5_out, Ir[0], Ir[1], not_6_out, Ir[3]);
  and and_6 (and_6_out, not_7_out, Ir[1], Ir[2], not_8_out, Ir[4], Ir[5], Ir[6], Ir[7]);
  D_Flip_Flop d_ff_4 (.D(and_4_out), .clk(clk), .Q(move), .reset(rst));  // open: Qn, preset
  D_Flip_Flop d_ff_5 (.D(and_5_out), .clk(clk), .Q(store), .reset(rst));  // open: Qn, preset
  D_Flip_Flop d_ff_6 (.D(and_6_out), .clk(clk), .Q(halt), .reset(rst));  // open: Qn, preset
  Register #(.width(2)) register_3 (.D(Ir[5:4]), .en(1'b1), .clk(clk), .Q(Rs), .clr(rst));
  D_Flip_Flop d_ff_7 (.D(1'b1), .clk(clk), .Q(d_ff_7_q), .reset(rst));  // open: Qn, preset
  nor nor_1 (nor_1_out, Ir[0], Ir[1]);
  D_Flip_Flop d_ff_8 (.D(nor_1_out), .clk(clk), .Q(d_ff_8_q), .reset(rst));  // open: Qn, preset
  D_Flip_Flop d_ff_9 (.D(d_ff_7_q), .clk(clk), .Q(d_ff_9_q), .reset(rst));  // open: Qn, preset
  and and_7 (jmp, d_ff_8_q, d_ff_9_q);

  // Other names for the same wires on the sheet: forhalt[7:0] = Ir; forjump[7:0] = Ir; zero = Ir[0]; first = Ir[1];
  //   second = Ir[2]; third = Ir[3]

  // Notes on the sheet:
  //   fv
endmodule

module TestJump (
  input  in_1,
  output [15:0] out_2,
  output [5:0] out_3
);

  wire clk, d_ff_1_q, d_ff_2_q, halt, id, idi, jmp, move, multiplexer_1_out, ovrfl, reg0WE, reg1WE, reg2WE,
       reg3WE, register_1_q, regwrite, store, subtrac;
  wire [1:0] Rd;
  wire [5:0] jmpaddress, programcounter_1_pc;
  wire [7:0] InstructionRegister_q, ram_1_dout;
  wire [15:0] A, B, data, DataRAM_dout, multiplexer_3_out, multiplexer_4_out, putput, R0, R1, R2, R3;
  wire [15:6] cyclecounter_1_cycles;

  Register #(.width(16)) u_R0 (.D(putput), .en(reg0WE), .clk(clk), .Q(R0), .clr(in_1));
  Register #(.width(16)) u_R1 (.D(putput), .en(reg1WE), .clk(clk), .Q(R1), .clr(in_1));
  Register #(.width(16)) u_R2 (.D(putput), .en(reg2WE), .clk(clk), .Q(R2), .clr(in_1));
  Register #(.width(16)) u_R3 (.D(putput), .en(reg3WE), .clk(clk), .Q(R3), .clr(in_1));
  Clock clock_1 (.out(clk));
  Hex_Digit_Display hex_digit_display_1 (.value(R0[15:12]));  // open: dp
  Hex_Digit_Display hex_digit_display_2 (.value(R0[11:8]));  // open: dp
  Hex_Digit_Display hex_digit_display_3 (.value(R2[15:12]));  // open: dp
  Hex_Digit_Display hex_digit_display_4 (.value(R2[11:8]));  // open: dp
  SubtractionOverflow subtractionoverflow_1 (.A(A), .OP(subtrac), .B(B), .out_4(data), .out_5(ovrfl));
  Hex_Digit_Display hex_digit_display_5 (.value(R0[7:4]));  // open: dp
  Hex_Digit_Display hex_digit_display_6 (.value(R2[7:4]));  // open: dp
  Hex_Digit_Display hex_digit_display_7 (.value(R0[3:0]));  // open: dp
  Hex_Digit_Display hex_digit_display_8 (.value(R2[3:0]));  // open: dp
  Hex_Digit_Display hex_digit_display_9 (.value(R1[15:12]));  // open: dp
  Hex_Digit_Display hex_digit_display_10 (.value(R1[11:8]));  // open: dp
  Hex_Digit_Display hex_digit_display_11 (.value(R3[15:12]));  // open: dp
  Hex_Digit_Display hex_digit_display_12 (.value(R3[11:8]));  // open: dp
  Hex_Digit_Display hex_digit_display_13 (.value(R1[7:4]));  // open: dp
  Hex_Digit_Display hex_digit_display_14 (.value(R3[7:4]));  // open: dp
  WriteEnableRegisters writeenableregisters_1 (
    .Rd(Rd), .regWrite(regwrite), .reg0WE(reg0WE), .reg1WE(reg1WE), .reg2WE(reg2WE), .reg3WE(reg3WE));
  Hex_Digit_Display hex_digit_display_15 (.value(R1[3:0]));  // open: dp
  Hex_Digit_Display hex_digit_display_16 (.value(R3[3:0]));  // open: dp
  Register #(.width(1)) register_1 (.D(regwrite), .en(ovrfl), .clk(clk), .Q(register_1_q), .clr(in_1));
  D_Flip_Flop d_ff_1 (.D(1'b1), .clk(clk), .Q(d_ff_1_q), .reset(in_1));  // open: Qn, preset
  LED led_1 (.in(register_1_q));
  D_Flip_Flop d_ff_2 (.D(d_ff_1_q), .clk(clk), .Q(d_ff_2_q), .reset(in_1));  // open: Qn, preset
  srcSel srcsel_1 (.sel(Rd), .reg0(R0), .reg1(R1), .reg2(R2), .reg3(R3), .out_6(A));
  srcSel srcsel_2 (.sel(out_2[1:0]), .reg0(R0), .reg1(R1), .reg2(R2), .reg3(R3), .out_6(B));
  Multiplexer multiplexer_1 (.in0(d_ff_2_q), .in1(1'b0), .out(multiplexer_1_out), .sel(store));
  Multiplexer multiplexer_2 (.in0(multiplexer_1_out), .in1(1'b0), .out(regwrite), .sel(jmp));
  programCounter programcounter_1 (
    .clk(clk), .rst(in_1), .jumpaddress(jmpaddress), .jump(jmp), .pc(programcounter_1_pc));  // open: jumpn
  RAM #(.addrWidth(4), .asyncread("true"), .dataWidth(16), .trigger("falling")) DataRAM (
    .addr(B[3:0]), .we(store), .oe(1'b1), .clk(clk), .din(A), .dout(DataRAM_dout));
  RAM #(.addrWidth(6), .asyncread("true"), .trigger("falling")) ram_1 (
    .addr(programcounter_1_pc), .we(1'b0), .oe(1'b1), .clk(clk), .dout(ram_1_dout));  // open: din
  cyclecounter cyclecounter_1 (.halt(halt), .clk(clk), .rst(in_1), .cycles({cyclecounter_1_cycles, out_3}));
  Register InstructionRegister (.D(ram_1_dout), .en(1'b1), .clk(clk), .Q(InstructionRegister_q), .clr(in_1));
  Multiplexer #(.width(16)) multiplexer_3 (.in0(data), .in1(DataRAM_dout), .out(multiplexer_3_out), .sel(id));
  Multiplexer #(.width(16)) multiplexer_4 (
    .in0(multiplexer_3_out), .in1({{14{1'b0}}, out_2[1:0]}), .out(multiplexer_4_out), .sel(idi));
  Multiplexer #(.width(16)) multiplexer_5 (.in0(multiplexer_4_out), .in1(B), .out(putput), .sel(move));
  IRDecoder4 irdecoder4_1 (
    .clk(clk), .rst(in_1), .Ir(InstructionRegister_q), .Rs(out_2[1:0]), .Rd(Rd), .subtrac(subtrac),
    .ldi(idi), .ld(id), .move(move), .store(store), .halt(halt), .jmpaddress(jmpaddress), .jmp(jmp));
  // Pins of 6 and 16 bits meet at {cyclecounter_1_cycles, out_3}

  assign out_2[15:2] = {14{1'b0}};

  // Other names for the same wires on the sheet: Rs[1:0] = out_2[1:0]; rst = in_1

  // Notes on the sheet:
  //   5341
  //   537d
  //   number is put here
  //   can be used to access
  //   4c41
  //   7b43
  //   address comes after you click once more on the number you get, so once u get 59, click one more and u get the right address 9.
  //   add
  //   subtract
  //   b3 43 e2 32 82
endmodule

module cyclecounter (
  input  halt,
  input  clk,
  input  rst,
  output [15:0] cycles
);

  wire not_1_out, register_1_q;
  wire [15:0] adder_1_out;

  Register #(.width(1)) register_1 (.D(1'b1), .en(halt), .clk(clk), .Q(register_1_q), .clr(rst));
  not not_1 (not_1_out, register_1_q);
  Register #(.width(16)) R0 (.D(adder_1_out), .en(not_1_out), .clk(clk), .Q(cycles), .clr(rst));
  Adder #(.width(16)) adder_1 (.a(cycles), .b(16'h1), .out(adder_1_out));  // open: cin, cout
endmodule

module ImprovedJump (
  input  in_1,
  output [15:0] out_2,
  output [5:0] out_3
);

  wire clk, d_ff_1_q, d_ff_2_q, d_ff_3_q, d_ff_4_q, halt, id, idi, jmp, move, multiplexer_1_out,
       multiplexer_2_out, multiplexer_3_out, ovrfl, reg0WE, reg1WE, reg2WE, reg3WE, register_1_q, regwrite,
       regwrite2, store, subtrac;
  wire [1:0] Rd;
  wire [5:0] jmpaddress, programcounter_1_pc;
  wire [7:0] InstructionRegister_q, ram_1_dout;
  wire [15:0] A, B, data, DataRAM_dout, multiplexer_5_out, multiplexer_6_out, putput, R0, R1, R2, R3;
  wire [15:6] cyclecounter_1_cycles;

  Register #(.width(16)) u_R0 (.D(putput), .en(reg0WE), .clk(clk), .Q(R0), .clr(in_1));
  Register #(.width(16)) u_R1 (.D(putput), .en(reg1WE), .clk(clk), .Q(R1), .clr(in_1));
  Register #(.width(16)) u_R2 (.D(putput), .en(reg2WE), .clk(clk), .Q(R2), .clr(in_1));
  Register #(.width(16)) u_R3 (.D(putput), .en(reg3WE), .clk(clk), .Q(R3), .clr(in_1));
  Clock clock_1 (.out(clk));
  Hex_Digit_Display hex_digit_display_1 (.value(R0[15:12]));  // open: dp
  Hex_Digit_Display hex_digit_display_2 (.value(R0[11:8]));  // open: dp
  Hex_Digit_Display hex_digit_display_3 (.value(R2[15:12]));  // open: dp
  Hex_Digit_Display hex_digit_display_4 (.value(R2[11:8]));  // open: dp
  SubtractionOverflow subtractionoverflow_1 (.A(A), .OP(subtrac), .B(B), .out_4(data), .out_5(ovrfl));
  Hex_Digit_Display hex_digit_display_5 (.value(R0[7:4]));  // open: dp
  Hex_Digit_Display hex_digit_display_6 (.value(R2[7:4]));  // open: dp
  Hex_Digit_Display hex_digit_display_7 (.value(R0[3:0]));  // open: dp
  Hex_Digit_Display hex_digit_display_8 (.value(R2[3:0]));  // open: dp
  Hex_Digit_Display hex_digit_display_9 (.value(R1[15:12]));  // open: dp
  Hex_Digit_Display hex_digit_display_10 (.value(R1[11:8]));  // open: dp
  Hex_Digit_Display hex_digit_display_11 (.value(R3[15:12]));  // open: dp
  Hex_Digit_Display hex_digit_display_12 (.value(R3[11:8]));  // open: dp
  Hex_Digit_Display hex_digit_display_13 (.value(R1[7:4]));  // open: dp
  Hex_Digit_Display hex_digit_display_14 (.value(R3[7:4]));  // open: dp
  WriteEnableRegisters writeenableregisters_1 (
    .Rd(Rd), .regWrite(regwrite), .reg0WE(reg0WE), .reg1WE(reg1WE), .reg2WE(reg2WE), .reg3WE(reg3WE));
  Hex_Digit_Display hex_digit_display_15 (.value(R1[3:0]));  // open: dp
  Hex_Digit_Display hex_digit_display_16 (.value(R3[3:0]));  // open: dp
  Register #(.width(1)) register_1 (.D(regwrite), .en(ovrfl), .clk(clk), .Q(register_1_q), .clr(in_1));
  D_Flip_Flop d_ff_1 (.D(1'b1), .clk(clk), .Q(d_ff_1_q), .reset(in_1));  // open: Qn, preset
  D_Flip_Flop d_ff_2 (.D(1'b1), .clk(clk), .Q(d_ff_2_q), .reset(in_1));  // open: Qn, preset
  LED led_1 (.in(register_1_q));
  D_Flip_Flop d_ff_3 (.D(d_ff_2_q), .clk(clk), .Q(d_ff_3_q), .reset(in_1));  // open: Qn, preset
  srcSel srcsel_1 (.sel(Rd), .reg0(R0), .reg1(R1), .reg2(R2), .reg3(R3), .out_6(A));
  srcSel srcsel_2 (.sel(out_2[1:0]), .reg0(R0), .reg1(R1), .reg2(R2), .reg3(R3), .out_6(B));
  Multiplexer multiplexer_1 (.in0(d_ff_1_q), .in1(1'b0), .out(multiplexer_1_out), .sel(store));
  Multiplexer multiplexer_2 (.in0(d_ff_3_q), .in1(1'b0), .out(multiplexer_2_out), .sel(store));
  Multiplexer multiplexer_3 (.in0(multiplexer_1_out), .in1(1'b0), .out(multiplexer_3_out), .sel(jmp));
  Multiplexer multiplexer_4 (.in0(multiplexer_2_out), .in1(1'b0), .out(regwrite), .sel(d_ff_4_q));
  D_Flip_Flop d_ff_4 (.D(jmp), .clk(clk), .Q(d_ff_4_q), .reset(in_1));  // open: Qn, preset
  programCounter programcounter_1 (
    .clk(clk), .rst(in_1), .jumpaddress(jmpaddress), .jump(jmp), .pc(programcounter_1_pc));  // open: jumpn
  D_Flip_Flop d_ff_5 (.D(multiplexer_3_out), .clk(clk), .Q(regwrite2), .reset(in_1));  // open: Qn, preset
  RAM #(.addrWidth(4), .asyncread("true"), .dataWidth(16), .trigger("falling")) DataRAM (
    .addr(B[3:0]), .we(store), .oe(1'b1), .clk(clk), .din(A), .dout(DataRAM_dout));
  RAM #(.addrWidth(6), .asyncread("true"), .trigger("falling")) ram_1 (
    .addr(programcounter_1_pc), .we(1'b0), .oe(1'b1), .clk(clk), .dout(ram_1_dout));  // open: din
  cyclecounter cyclecounter_1 (.halt(halt), .clk(clk), .rst(in_1), .cycles({cyclecounter_1_cycles, out_3}));
  Register InstructionRegister (.D(ram_1_dout), .en(1'b1), .clk(clk), .Q(InstructionRegister_q), .clr(in_1));
  Multiplexer #(.width(16)) multiplexer_5 (.in0(data), .in1(DataRAM_dout), .out(multiplexer_5_out), .sel(id));
  Multiplexer #(.width(16)) multiplexer_6 (
    .in0(multiplexer_5_out), .in1({{14{1'b0}}, out_2[1:0]}), .out(multiplexer_6_out), .sel(idi));
  Multiplexer #(.width(16)) multiplexer_7 (.in0(multiplexer_6_out), .in1(B), .out(putput), .sel(move));
  IRDecoder5 irdecoder5_1 (
    .clk(clk), .rst(in_1), .Ir(InstructionRegister_q), .Rs(out_2[1:0]), .Rd(Rd), .subtrac(subtrac),
    .ldi(idi), .ld(id), .move(move), .store(store), .halt(halt), .jmpaddress(jmpaddress), .jmp(jmp));
  // Pins of 6 and 16 bits meet at {cyclecounter_1_cycles, out_3}

  assign out_2[15:2] = {14{1'b0}};

  // Other names for the same wires on the sheet: Rs[1:0] = out_2[1:0]; rst = in_1

  // Notes on the sheet:
  //   5341
  //   537d
  //   number is put here
  //   can be used to access
  //   4c41
  //   7b43
  //   address comes after you click once more on the number you get, so once u get 59, click one more and u get the right address 9.
  //   add
  //   subtract
  //   does not work lmao lil bro ur horrible at the game + ratio + get better + get a life + idk 
  //   b3 43 e2 32 82
endmodule

module IRDecoder5 (
  input  clk,
  input  rst,
  input  [7:0] Ir,
  output [1:0] Rs,
  output [1:0] Rd,
  output subtrac,
  output ldi,
  output ld,
  output move,
  output store,
  output halt,
  output [5:0] jmpaddress,
  output jmp
);

  wire and_1_out, and_2_out, and_3_out, and_4_out, and_5_out, and_6_out, d_ff_7_q, d_ff_8_q, nor_1_out,
       not_1_out, not_2_out, not_3_out, not_4_out, not_5_out, not_6_out, not_7_out, not_8_out;

  not not_1 (not_1_out, Ir[2]);
  not not_2 (not_2_out, Ir[3]);
  not not_3 (not_3_out, Ir[0]);
  not not_4 (not_4_out, Ir[0]);
  not not_5 (not_5_out, Ir[3]);
  not not_6 (not_6_out, Ir[2]);
  not not_7 (not_7_out, Ir[0]);
  Register #(.width(2)) register_1 (.D(Ir[7:6]), .en(1'b1), .clk(clk), .Q(Rd), .clr(rst));
  and and_1 (and_1_out, Ir[0], Ir[1], not_1_out, not_2_out);
  and and_2 (and_2_out, not_3_out, Ir[1], Ir[2], Ir[3]);
  not not_8 (not_8_out, Ir[3]);
  D_Flip_Flop d_ff_1 (.D(and_1_out), .clk(clk), .Q(subtrac), .reset(rst));  // open: Qn, preset
  D_Flip_Flop d_ff_2 (.D(and_2_out), .clk(clk), .Q(ldi), .reset(rst));  // open: Qn, preset
  D_Flip_Flop d_ff_3 (.D(and_3_out), .clk(clk), .Q(ld), .reset(rst));  // open: Qn, preset
  and and_3 (and_3_out, Ir[0], Ir[1], Ir[2], Ir[3]);
  and and_4 (and_4_out, not_4_out, Ir[1], Ir[2], not_5_out);
  and and_5 (and_5_out, Ir[0], Ir[1], not_6_out, Ir[3]);
  and and_6 (and_6_out, not_7_out, Ir[1], Ir[2], not_8_out, Ir[4], Ir[5], Ir[6], Ir[7]);
  D_Flip_Flop d_ff_4 (.D(and_4_out), .clk(clk), .Q(move), .reset(rst));  // open: Qn, preset
  D_Flip_Flop d_ff_5 (.D(and_5_out), .clk(clk), .Q(store), .reset(rst));  // open: Qn, preset
  D_Flip_Flop d_ff_6 (.D(and_6_out), .clk(clk), .Q(halt), .reset(rst));  // open: Qn, preset
  Register #(.width(2)) register_2 (.D(Ir[5:4]), .en(1'b1), .clk(clk), .Q(Rs), .clr(rst));
  nor nor_1 (nor_1_out, Ir[0], Ir[1]);
  D_Flip_Flop d_ff_7 (.D(1'b1), .clk(clk), .Q(d_ff_7_q), .reset(rst));  // open: Qn, preset
  D_Flip_Flop d_ff_8 (.D(d_ff_7_q), .clk(clk), .Q(d_ff_8_q), .reset(rst));  // open: Qn, preset
  and and_7 (jmp, nor_1_out, d_ff_8_q);

  assign jmpaddress = Ir[7:2];

  // Other names for the same wires on the sheet: forhalt[7:0] = Ir; forjump[7:0] = Ir; zero = Ir[0]; first = Ir[1];
  //   second = Ir[2]; third = Ir[3]

  // Notes on the sheet:
  //   fv
endmodule

module ConditionalJump (
  input  in_1,
  output [15:0] out_2,
  output [15:0] out_3
);

  wire and_1_out, and_2_out, clk, d_ff_1_q, d_ff_2_q, d_ff_3_q, d_ff_4_q, d_ff_5_q, d_ff_6_q, d_ff_7_q,
       d_ff_9_q, halt, id, idi, jmp, jmpn, move, multiplexer_1_out, multiplexer_2_out, multiplexer_3_out,
       multiplexer_4_out, multiplexer_5_out, not_1_out, not_2_out, or_1_out, ovrfl, reg0WE, reg1WE, reg2WE,
       reg3WE, register_1_q, regwrite, regwrite1, regwrite2, store, subtrac;
  wire [1:0] Rd;
  wire [5:0] jmpaddress, programcounter_1_pc;
  wire [7:0] decode, InstructionRegister_q, ram_1_dout;
  wire [15:0] A, B, data, DataRAM_dout, multiplexer_8_out, multiplexer_9_out, putput, R0, R1, R2, R3;

  Register #(.width(16)) u_R0 (.D(putput), .en(reg0WE), .clk(clk), .Q(R0), .clr(in_1));
  Register #(.width(16)) u_R1 (.D(putput), .en(reg1WE), .clk(clk), .Q(R1), .clr(in_1));
  Register #(.width(16)) u_R2 (.D(putput), .en(reg2WE), .clk(clk), .Q(R2), .clr(in_1));
  Register #(.width(16)) u_R3 (.D(putput), .en(reg3WE), .clk(clk), .Q(R3), .clr(in_1));
  Clock clock_1 (.out(clk));
  Hex_Digit_Display hex_digit_display_1 (.value(R0[15:12]));  // open: dp
  Hex_Digit_Display hex_digit_display_2 (.value(R0[11:8]));  // open: dp
  Hex_Digit_Display hex_digit_display_3 (.value(R2[15:12]));  // open: dp
  Hex_Digit_Display hex_digit_display_4 (.value(R2[11:8]));  // open: dp
  SubtractionOverflow subtractionoverflow_1 (.A(A), .OP(subtrac), .B(B), .out_4(data), .out_5(ovrfl));
  Hex_Digit_Display hex_digit_display_5 (.value(R0[7:4]));  // open: dp
  Hex_Digit_Display hex_digit_display_6 (.value(R2[7:4]));  // open: dp
  Hex_Digit_Display hex_digit_display_7 (.value(R0[3:0]));  // open: dp
  Hex_Digit_Display hex_digit_display_8 (.value(R2[3:0]));  // open: dp
  Hex_Digit_Display hex_digit_display_9 (.value(R1[15:12]));  // open: dp
  Hex_Digit_Display hex_digit_display_10 (.value(R1[11:8]));  // open: dp
  Hex_Digit_Display hex_digit_display_11 (.value(R3[15:12]));  // open: dp
  Hex_Digit_Display hex_digit_display_12 (.value(R3[11:8]));  // open: dp
  not not_1 (not_1_out, move);
  Hex_Digit_Display hex_digit_display_13 (.value(R1[7:4]));  // open: dp
  Hex_Digit_Display hex_digit_display_14 (.value(R3[7:4]));  // open: dp
  WriteEnableRegisters writeenableregisters_1 (
    .Rd(Rd), .regWrite(regwrite), .reg0WE(reg0WE), .reg1WE(reg1WE), .reg2WE(reg2WE), .reg3WE(reg3WE));
  and and_1 (and_1_out, not_1_out, ovrfl);
  Hex_Digit_Display hex_digit_display_15 (.value(R1[3:0]));  // open: dp
  Hex_Digit_Display hex_digit_display_16 (.value(R3[3:0]));  // open: dp
  Register #(.width(1)) register_1 (.D(regwrite), .en(and_1_out), .clk(clk), .Q(register_1_q), .clr(in_1));
  D_Flip_Flop d_ff_1 (.D(1'b1), .clk(clk), .Q(d_ff_1_q), .reset(in_1));  // open: Qn, preset
  D_Flip_Flop d_ff_2 (.D(1'b1), .clk(clk), .Q(d_ff_2_q), .reset(in_1));  // open: Qn, preset
  D_Flip_Flop d_ff_3 (.D(1'b1), .clk(clk), .Q(d_ff_3_q), .reset(in_1));  // open: Qn, preset
  LED led_1 (.in(register_1_q));
  D_Flip_Flop d_ff_4 (.D(d_ff_2_q), .clk(clk), .Q(d_ff_4_q), .reset(in_1));  // open: Qn, preset
  D_Flip_Flop d_ff_5 (.D(d_ff_3_q), .clk(clk), .Q(d_ff_5_q), .reset(in_1));  // open: Qn, preset
  srcSel srcsel_1 (.sel(Rd), .reg0(R0), .reg1(R1), .reg2(R2), .reg3(R3), .out_6(A));
  or or_1 (or_1_out, jmpn, jmp);
  srcSel srcsel_2 (.sel(out_2[1:0]), .reg0(R0), .reg1(R1), .reg2(R2), .reg3(R3), .out_6(B));
  cyclecounter cyclecounter_1 (.halt(halt), .clk(clk), .rst(in_1), .cycles(out_3));
  Multiplexer multiplexer_1 (.in0(d_ff_1_q), .in1(1'b0), .out(multiplexer_1_out), .sel(store));
  Multiplexer multiplexer_2 (.in0(d_ff_4_q), .in1(1'b0), .out(multiplexer_2_out), .sel(store));
  Multiplexer multiplexer_3 (.in0(d_ff_5_q), .in1(1'b0), .out(multiplexer_3_out), .sel(store));
  Multiplexer multiplexer_4 (.in0(multiplexer_1_out), .in1(1'b0), .out(multiplexer_4_out), .sel(jmp));
  Multiplexer multiplexer_5 (.in0(multiplexer_2_out), .in1(1'b0), .out(multiplexer_5_out), .sel(d_ff_6_q));
  D_Flip_Flop d_ff_6 (.D(jmp), .clk(clk), .Q(d_ff_6_q), .reset(in_1));  // open: Qn, preset
  not not_2 (not_2_out, decode[1]);
  Multiplexer multiplexer_6 (.in0(multiplexer_3_out), .in1(1'b0), .out(regwrite1), .sel(d_ff_7_q));
  D_Flip_Flop d_ff_7 (.D(or_1_out), .clk(clk), .Q(d_ff_7_q), .reset(in_1));  // open: Qn, preset
  D_Flip_Flop d_ff_8 (.D(multiplexer_4_out), .clk(clk), .Q(regwrite2), .reset(in_1));  // open: Qn, preset
  and and_2 (and_2_out, decode[0], not_2_out);
  RAM #(.addrWidth(7), .asyncread("true"), .dataWidth(16), .trigger("falling")) DataRAM (
    .addr(B[6:0]), .we(store), .oe(1'b1), .clk(clk), .din(A), .dout(DataRAM_dout));
  programCounter programcounter_1 (
    .clk(clk), .rst(in_1), .jumpaddress(jmpaddress), .jump(jmp), .jumpn(jmpn), .pc(programcounter_1_pc));
  D_Flip_Flop d_ff_9 (.D(and_2_out), .clk(clk), .Q(d_ff_9_q), .reset(in_1));  // open: Qn, preset
  RAM #(.addrWidth(6), .asyncread("true"), .trigger("falling")) ram_1 (
    .addr(programcounter_1_pc), .we(1'b0), .oe(1'b1), .clk(clk), .dout(ram_1_dout));  // open: din
  Multiplexer multiplexer_7 (.in0(multiplexer_5_out), .in1(1'b0), .out(regwrite), .sel(d_ff_9_q));
  Multiplexer #(.width(16)) multiplexer_8 (.in0(data), .in1(DataRAM_dout), .out(multiplexer_8_out), .sel(id));
  Register InstructionRegister (.D(ram_1_dout), .en(1'b1), .clk(clk), .Q(InstructionRegister_q), .clr(in_1));
  Multiplexer #(.width(16)) multiplexer_9 (
    .in0(multiplexer_8_out), .in1({{14{1'b0}}, out_2[1:0]}), .out(multiplexer_9_out), .sel(idi));
  Multiplexer #(.width(16)) multiplexer_10 (.in0(multiplexer_9_out), .in1(B), .out(putput), .sel(move));
  IRDecoder6 irdecoder6_1 (
    .clk(clk), .rst(in_1), .Ir(InstructionRegister_q), .negative(putput[15]), .Rs(out_2[1:0]), .Rd(Rd),
    .decode(decode), .subtrac(subtrac), .ldi(idi), .ld(id), .move(move), .store(store), .halt(halt),
    .jmpn(jmpn), .jmpaddress(jmpaddress), .jmp(jmp));

  assign out_2[15:2] = {14{1'b0}};

  // Other names for the same wires on the sheet: Rs[1:0] = out_2[1:0]; rst = in_1

  // Notes on the sheet:
  //   5341
  //   537d
  //   number is put here
  //   can be used to access
  //   4c41
  //   7b43
  //   address comes after you click once more on the number you get, so once u get 59, click one more and u get the right address 9.
  //   add
  //   subtract
  //   even if it doesnt jump, it still needs a cycle where nothing is written to register aka one more instruction.
  //   does not work lmao lil bro ur horrible at the game + ratio + get better + get a life + idk 
  //   b3 43 e2 32 82
endmodule

module IRDecoder6 (
  input  clk,
  input  rst,
  input  [7:0] Ir,
  input  negative,
  output [1:0] Rs,
  output [1:0] Rd,
  output [7:0] decode,
  output subtrac,
  output ldi,
  output ld,
  output move,
  output store,
  output halt,
  output jmpn,
  output [5:0] jmpaddress,
  output jmp
);

  wire and_1_out, and_2_out, and_3_out, and_4_out, and_5_out, and_6_out, d_ff_7_q, fv, nor_1_out, not_1_out,
       not_2_out, not_3_out, not_4_out, not_5_out, not_6_out, not_7_out, not_8_out, not_9_out;

  not not_1 (not_1_out, Ir[2]);
  not not_2 (not_2_out, Ir[3]);
  not not_3 (not_3_out, Ir[0]);
  not not_4 (not_4_out, Ir[0]);
  not not_5 (not_5_out, Ir[3]);
  not not_6 (not_6_out, Ir[2]);
  not not_7 (not_7_out, Ir[0]);
  Register #(.width(2)) register_1 (.D(Ir[7:6]), .en(1'b1), .clk(clk), .Q(Rd), .clr(rst));
  and and_1 (and_1_out, Ir[0], Ir[1], not_1_out, not_2_out);
  and and_2 (and_2_out, not_3_out, Ir[1], Ir[2], Ir[3]);
  not not_8 (not_8_out, Ir[3]);
  not not_9 (not_9_out, Ir[1]);
  D_Flip_Flop d_ff_1 (.D(and_1_out), .clk(clk), .Q(subtrac), .reset(rst));  // open: Qn, preset
  D_Flip_Flop d_ff_2 (.D(and_2_out), .clk(clk), .Q(ldi), .reset(rst));  // open: Qn, preset
  D_Flip_Flop d_ff_3 (.D(and_3_out), .clk(clk), .Q(ld), .reset(rst));  // open: Qn, preset
  and and_3 (and_3_out, Ir[0], Ir[1], Ir[2], Ir[3]);
  and and_4 (and_4_out, not_4_out, Ir[1], Ir[2], not_5_out);
  and and_5 (and_5_out, Ir[0], Ir[1], not_6_out, Ir[3]);
  and and_6 (and_6_out, not_7_out, Ir[1], Ir[2], not_8_out, Ir[4], Ir[5], Ir[6], Ir[7]);
  D_Flip_Flop d_ff_4 (.D(and_4_out), .clk(clk), .Q(move), .reset(rst));  // open: Qn, preset
  D_Flip_Flop d_ff_5 (.D(and_5_out), .clk(clk), .Q(store), .reset(rst));  // open: Qn, preset
  D_Flip_Flop d_ff_6 (.D(and_6_out), .clk(clk), .Q(halt), .reset(rst));  // open: Qn, preset
  Register #(.width(2)) register_2 (.D(Ir[5:4]), .en(1'b1), .clk(clk), .Q(Rs), .clr(rst));
  and and_7 (jmpn, Ir[0], negative, fv, not_9_out);
  nor nor_1 (nor_1_out, Ir[0], Ir[1]);
  D_Flip_Flop d_ff_7 (.D(1'b1), .clk(clk), .Q(d_ff_7_q), .reset(rst));  // open: Qn, preset
  D_Flip_Flop d_ff_8 (.D(d_ff_7_q), .clk(clk), .Q(fv), .reset(rst));  // open: Qn, preset
  and and_8 (jmp, nor_1_out, fv);

  assign decode = Ir;
  assign jmpaddress = Ir[7:2];

  // Other names for the same wires on the sheet: forhalt[7:0] = Ir; forjump[7:0] = Ir; zero = Ir[0]; first = Ir[1];
  //   second = Ir[2]; third = Ir[3]; neg = negative

  // Notes on the sheet:
  //   fv
endmodule
